# Fritzing sketch Circuit (saved by Fritzing 0.9.6b)
breadboards: 2

parts:
  Part1 = Arduino Pro Mini (5V)
  M1 = Niren can bus module [package=THT]
  M2 = Niren can bus module [package=THT]
  R1 = Resistor [tolerance=±5% power=0.25 resistance=220 package=THT]
  LED1 = LED - 5mm [color="White (4500K)" current=0.030 package="5 mm [THT]"]
  S1 = Pushbutton [package="[THT]"]
  Part2 = Arduino Pro Mini (5V)

nets:
  N1: Part1.GND, M1.pin2, R1.Pin_0
  N2: Part1.VCC, M1.pin1
  N3: Part1.SCK, M1.pin6
  N4: Part1.MISO, M1.pin4
  N5: Part1.MOSI, M1.pin5
  N6: Part1.D10, M1.pin3
  N7: Part1.D9, LED1.anode
  N8: Part1.D2, M1.pin7
  N9: M1.pin8, M1.pin9
  N10: M1.pin10, M1.pin12, M2.pin10, M2.pin12
  N11: M1.pin13, M2.pin13
  N12: M2.pin1, Part2.VCC
  N13: M2.pin2, S1.Pin_1, S1.Pin_2, Part2.GND
  N14: M2.pin3, Part2.D10
  N15: M2.pin4, Part2.MISO
  N16: M2.pin5, Part2.MOSI
  N17: M2.pin6, Part2.SCK
  N18: M2.pin7, Part2.D2
  N19: M2.pin8, M2.pin9
  N20: R1.Pin_1, LED1.cathode
  N21: S1.Pin_3, S1.Pin_4, Part2.D9

custom parts:
  Niren can bus module: Niren can bus module availabe on ebay and others. No pcb view as no mechanical drawng and it wouldn't mount anyway.
